// Logisim project control-logic.circ as structural Verilog: 1 circuit, main circuit control_logic
module control_logic (
  input  [31:0] Instruction,
  input  BrEq,
  input  BrLt,
  output PCSel,
  output RegWEn,
  output [2:0] ImmSel,
  output BrUn,
  output ASel,
  output BSel,
  output [3:0] ALUSel,
  output MemWEn,
  output [1:0] WBSel
);

  wire add_r, and_11_out, and_12_out, and_13_out, and_14_out, and_r, auipc, B_inst, beq, bge, bgeu, blt,
       bltu, bne, demultiplexer_1_out5, funct3_0, funct3_1, funct3_2, i_addi, i_andi, i_ori, i_slli, i_slti,
       i_srai, i_srli, i_xori, is_add_r, is_i_3, is_i_8, is_mul_r, is_mulh_r, is_sll_r, is_sra_r, is_srai_7,
       is_srl_r, is_srli_7, is_sub_r, jal, jalr, lb, lh, lui, lw, mul_r, mulh_r, mulhu_r, not_1_out,
       not_2_out, opcode3, opcode23, opcode67, or_1_out, or_2_out, or_3_out, or_r, r_0, r_1, r_5, Rinst, sb,
       sh, sll_r, slt_r, sra_r, srl_r, sub_r, sw, xor_r;
  wire [5:0] rom_input;
  wire [6:0] undriven;
  wire [15:14] rom_1_data;

  Comparator #(.width(3)) comparator_1 (.a(Instruction[14:12]), .b(3'b011), .eq(is_i_3));  // open: gt, lt
  Comparator #(.width(7)) comparator_2 (.a(Instruction[31:25]), .b(7'b0100000), .eq(is_sub_r));  // open: gt, lt
  Comparator #(.width(7)) comparator_3 (.a(undriven), .b({7{1'b0}}), .eq(is_add_r));  // open: gt, lt
  Comparator #(.width(7)) comparator_4 (.a(Instruction[31:25]), .b(7'b0000001), .eq(is_mul_r));  // open: gt, lt
  Comparator #(.width(7)) comparator_5 (.a(Instruction[31:25]), .b({7{1'b0}}), .eq(is_srl_r));  // open: gt, lt
  Comparator #(.width(7)) comparator_6 (.a(Instruction[31:25]), .b({7{1'b0}}), .eq(is_sll_r));  // open: gt, lt
  Comparator #(.width(7)) comparator_7 (.a(Instruction[6:0]), .b(7'b0110011), .eq(Rinst));  // open: gt, lt
  Comparator #(.width(7)) comparator_8 (.a(Instruction[31:25]), .b(7'b0100000), .eq(is_sra_r));  // open: gt, lt
  Comparator #(.width(7)) comparator_9 (.a(Instruction[31:25]), .b(7'b0000001), .eq(is_mulh_r));  // open: gt, lt
  Comparator #(.width(7)) comparator_10 (.a(Instruction[6:0]), .b(7'b1101111), .eq(jal));  // open: gt, lt
  Comparator #(.width(7)) comparator_11 (.a(Instruction[6:0]), .b(7'b1100111), .eq(opcode67));  // open: gt, lt
  ROM #(.addrWidth(6), .dataWidth(16)) rom_1 (
    .addr(rom_input), .data({rom_1_data, WBSel, MemWEn, ALUSel, BSel, ASel, BrUn, ImmSel, RegWEn}));
  Demultiplexer #(.select(3)) demultiplexer_1 (
    .out0(i_addi), .out1(i_slli), .out2(i_slti), .out4(i_xori), .out5(demultiplexer_1_out5), .out6(i_ori),
    .out7(i_andi), .in(is_i_8), .sel(Instruction[14:12]));  // open: out3
  Comparator #(.width(7)) comparator_12 (.a(Instruction[6:0]), .b(7'b0010111), .eq(auipc));  // open: gt, lt
  Comparator #(.width(7)) comparator_13 (.a(Instruction[6:0]), .b(7'b0110111), .eq(lui));  // open: gt, lt
  Comparator #(.width(7)) comparator_14 (.a(Instruction[6:0]), .b(7'b0010011), .eq(is_i_8));  // open: gt, lt
  Comparator #(.width(7)) comparator_15 (.a(Instruction[31:25]), .b({7{1'b0}}), .eq(is_srli_7));  // open: gt, lt
  Comparator #(.width(7)) comparator_16 (.a(Instruction[31:25]), .b(7'b0100000), .eq(is_srai_7));  // open: gt, lt
  Demultiplexer #(.select(3)) demultiplexer_2 (
    .out0(r_0), .out1(r_1), .out2(slt_r), .out3(mulhu_r), .out4(xor_r), .out5(r_5), .out6(or_r),
    .out7(and_r), .in(Rinst), .sel(Instruction[14:12]));
  and and_1 (i_srli, demultiplexer_1_out5, is_srli_7);
  and and_2 (sub_r, r_0, is_sub_r);
  and and_3 (add_r, r_0, is_add_r);
  and and_4 (mul_r, is_mul_r, r_0);
  and and_5 (sll_r, is_sll_r, r_1);
  and and_6 (mulh_r, r_1, is_mulh_r);
  and and_7 (srl_r, is_srl_r, r_5);
  and and_8 (sra_r, r_5, is_sra_r);
  and and_9 (jalr, funct3_0, opcode67);
  and and_10 (i_srai, demultiplexer_1_out5, is_srai_7);
  Demultiplexer #(.select(3)) demultiplexer_3 (
    .out0(beq), .out1(bne), .out4(blt), .out5(bge), .out6(bltu), .out7(bgeu), .in(B_inst),
    .sel(Instruction[14:12]));  // open: out2, out3
  Comparator #(.width(7)) comparator_17 (.a(Instruction[6:0]), .b(7'b1100011), .eq(B_inst));  // open: gt, lt
  or or_1 (or_1_out, blt, bltu);
  not not_1 (not_1_out, BrEq);
  not not_2 (not_2_out, BrLt);
  and and_11 (and_11_out, or_1_out, BrLt);
  and and_12 (and_12_out, BrEq, beq);
  or or_2 (or_2_out, jal, jalr);
  and and_13 (and_13_out, not_1_out, bne);
  or or_3 (or_3_out, bgeu, bge);
  and and_14 (and_14_out, or_3_out, not_2_out);
  Comparator #(.width(7)) comparator_18 (.a(Instruction[6:0]), .b(7'b0000011), .eq(opcode3));  // open: gt, lt
  Comparator #(.width(3)) comparator_19 (.a(Instruction[14:12]), .b(3'b000), .eq(funct3_0));  // open: gt, lt
  Comparator #(.width(3)) comparator_20 (.a(Instruction[14:12]), .b(3'b001), .eq(funct3_1));  // open: gt, lt
  Comparator #(.width(3)) comparator_21 (.a(Instruction[14:12]), .b(3'b010), .eq(funct3_2));  // open: gt, lt
  Comparator #(.width(7)) comparator_22 (.a(Instruction[6:0]), .b(7'b0100011), .eq(opcode23));  // open: gt, lt
  Priority_Encoder #(.select_enc(6)) priority_encoder_1 (
    .in0(add_r), .in1(mul_r), .in2(sub_r), .in3(sll_r), .in4(mulh_r), .in5(mulhu_r), .in6(slt_r),
    .in7(xor_r), .in8(srl_r), .in9(sra_r), .in10(or_r), .in11(and_r), .in12(lh), .in13(lb), .in14(lw),
    .in15(i_addi), .in16(i_slli), .in17(i_slti), .in18(i_xori), .in19(i_srli), .in20(i_srai), .in21(i_ori),
    .in22(i_andi), .in23(sw), .in24(sb), .in25(sh), .in26(bne), .in27(beq), .in28(blt), .in29(bge),
    .in30(bltu), .in31(bgeu), .in32(auipc), .in33(lui), .in34(jal), .in35(jalr), .out(rom_input));  // open: in36, in37, in38, in39, in40, in41, in42, in43, in44, in45, in46, in47, in48, in49, in50, in51, in52, in53, in54, in55, in56, in57, in58, in59, in60, in61, in62, in63, gs, en_out, en_in
  or or_4 (PCSel, and_11_out, and_12_out, or_2_out, and_13_out, and_14_out);
  and and_15 (lb, funct3_0, opcode3);
  and and_16 (sb, funct3_0, opcode23);
  and and_17 (sh, funct3_1, opcode23);
  and and_18 (sw, funct3_2, opcode23);
  and and_19 (lh, funct3_1, opcode3);
  and and_20 (lw, funct3_2, opcode3);

  // Other names for the same wires on the sheet: opcode[6:0] = Instruction[6:0];
  //   Unused[14:0] = {Instruction[24:15], Instruction[11:7]}; funct3[2:0] = Instruction[14:12];
  //   funct7[6:0] = Instruction[31:25]; opcode6f = jal; opcode17 = auipc; opcode37 = lui

  // Notes on the sheet:
  //   INPUTS to your circuit
  //   Connect ROM Input here ->
  //   contents of rom_1 (hex, n*v repeats v):
  //   1001 1401 1601 1081 1481 1581 1101 1201 1281 1681 1301 1381 41 41 41 1041 10c1 1141 1241 12c1 16c1
  //   1341 13c1 3842 3842 3842 4*3064 1074 1074 1067 17e7 2069 2041
  //   ROM FOR CONTROL LOGIC
  //   DON'T CHANGE THE LOCATIONS OF THE INPUTS AND OUTPUTS!
  //   This is only if you choose to do the ROM option
  //   CONNECT
  //   WIRE
  //   TO
  //   USE
  //   ROM
  //   OUTPUT from your circuit
  //   Reminder: If using ROM, use combinational logic for PCSel
endmodule
