// Logisim project cpu.circ as structural Verilog: 1 circuit, main circuit cpu
module cpu (
  input  clk,
  input  [31:0] Instruction,
  input  [31:0] MemReadData,
  output [31:0] MemAddress,
  output [31:0] ProgramCounter,
  output [31:0] ra,
  output [31:0] sp,
  output [31:0] t0,
  output [31:0] t1,
  output [31:0] t2,
  output [31:0] s0,
  output [31:0] s1,
  output [31:0] a0,
  output [3:0] MemWriteMask,
  output [31:0] MemWriteData
);

  wire asel, brEq, brLt, brUn, bsel, memWEn, pcSel, regWEn;
  wire [1:0] wbSel;
  wire [2:0] immSel;
  wire [3:0] aluSel;
  wire [11:0] imm;
  wire [19:0] pipelineInst;
  wire [31:0] adder_1_out, adder_2_out, dataToReg, imm_output, multiplexer_1_out, multiplexer_2_out,
       multiplexer_3_out, multiplexer_4_out, multiplexer_5_out, pipelinePC, ReadData1, ReadData2;

  Adder #(.width(32)) adder_1 (.a(ProgramCounter), .b(32'h4), .out(adder_1_out));  // open: cin, cout
  Multiplexer #(.width(32)) multiplexer_1 (.in0(adder_1_out), .in1(MemAddress), .out(multiplexer_1_out), .sel(pcSel));
  Register #(.width(32)) register_1 (.D(multiplexer_1_out), .clk(clk), .Q(ProgramCounter));  // open: en, clr
  Register #(.width(32)) register_2 (.D(ProgramCounter), .clk(clk), .Q(pipelinePC));  // open: en, clr
  Multiplexer #(.width(32)) multiplexer_2 (.in0(Instruction), .in1(32'h13), .out(multiplexer_2_out), .sel(pcSel));
  Register #(.width(32)) register_3 (.D(multiplexer_2_out), .clk(clk), .Q({imm, pipelineInst}));  // open: en, clr
  Adder #(.width(32)) adder_2 (.a(pipelinePC), .b(32'h4), .out(adder_2_out));  // open: cin, cout
  Multiplexer #(.select(2), .width(32)) multiplexer_3 (
    .in0(dataToReg), .in1(MemAddress), .in2(adder_2_out), .out(multiplexer_3_out), .sel(wbSel));  // open: in3
  control_logic control_logic_1 (
    .Instruction({imm, pipelineInst}), .BrEq(brEq), .BrLt(brLt), .PCSel(pcSel), .RegWEn(regWEn),
    .ImmSel(immSel), .BrUn(brUn), .ASel(asel), .BSel(bsel), .ALUSel(aluSel), .MemWEn(memWEn), .WBSel(wbSel));
  regfile regfile_1 (
    .ReadIndex1(pipelineInst[19:15]), .ReadIndex2(imm[4:0]), .WriteIndex(pipelineInst[11:7]),
    .WriteData(multiplexer_3_out), .RegWEn(regWEn), .clk(clk), .ra(ra), .sp(sp), .t0(t0), .t1(t1), .t2(t2),
    .s0(s0), .s1(s1), .a0(a0), .ReadData1(ReadData1), .ReadData2(ReadData2));
  imm_gen imm_gen_1 (.Instruction({imm, pipelineInst}), .ImmSel(immSel), .Immediate(imm_output));
  Multiplexer #(.width(32)) multiplexer_4 (.in0(ReadData1), .in1(pipelinePC), .out(multiplexer_4_out), .sel(asel));
  Multiplexer #(.width(32)) multiplexer_5 (.in0(ReadData2), .in1(imm_output), .out(multiplexer_5_out), .sel(bsel));
  alu alu_1 (.A(multiplexer_4_out), .B(multiplexer_5_out), .ALUSel(aluSel), .ALUResult(MemAddress));
  branch_comp branch_comp_1 (.BrData1(ReadData1), .BrData2(ReadData2), .BrUn(brUn), .BrEq(brEq), .BrLt(brLt));
  partial_store partial_store_1 (
    .Instruction({imm, pipelineInst}), .MemAddress(MemAddress), .DataFromReg(ReadData2), .MemWEn(memWEn),
    .MemWriteMask(MemWriteMask), .DataToMem(MemWriteData));
  partial_load partial_load_1 (
    .Instruction({imm, pipelineInst}), .MemAddress(MemAddress), .DataFromMem(MemReadData),
    .DataToReg(dataToReg));

  // Other names for the same wires on the sheet: ALUResult[31:0] = MemAddress; unused1[6:0] = pipelineInst[6:0];
  //   rd[4:0] = pipelineInst[11:7]; unused2[2:0] = pipelineInst[14:12]; rs1[4:0] = pipelineInst[19:15];
  //   pipelineInst[31:20] = imm; rs2[4:0] = imm[4:0]; unused3[6:0] = imm[11:5]; TO_IMEM[31:0] = ProgramCounter

  // Notes on the sheet:
  //   To IMEM
  //   IMEM (do **NOT** move this)
  //   From IMEM
  //   Inputs/Outputs for testing. Do **NOT** move these.
  //   It is OK to move the PC, RegFile, ALU, MEM, Branch Comp, Imm Gen, Partial Load, Partial Store and Control Logic to wherever is most convenient for you when constructing your CPU, and to delete this text
  //   To DMEM
  //   DMEM (do **NOT** move this)
  //   From DMEM
endmodule
