// Logisim project partial-store.circ as structural Verilog: 1 circuit, main circuit partial_store
module partial_store (
  input  [31:0] Instruction,
  input  [31:0] MemAddress,
  input  [31:0] DataFromReg,
  input  MemWEn,
  output [3:0] MemWriteMask,
  output [31:0] DataToMem
);

  wire and_1_out, and_2_out, and_3_out, and_4_out, and_5_out, and_6_out, and_7_out, bot_0, bot_1, bot_2,
       bot_3, funct3_is_0, funct3_is_1, funct3_is_2;
  wire [3:0] priority_encoder_1_out;
  wire [7:0] e;
  wire [15:0] sixteen;
  wire [23:0] bit_extender_2_out;
  wire [31:0] data0_7, data15_0, store_half, storebyte;

  assign data0_7 = {{24{DataFromReg[7]}}, DataFromReg[7:0]};  // Bit_Extender bit_extender_1
  assign bit_extender_2_out = {{23{1'b0}}, 1'b0};  // Bit_Extender bit_extender_2
  Multiplexer #(.select(2), .width(32)) multiplexer_1 (
    .in0({bit_extender_2_out, data0_7[7:0]}), .in1({e, e, data0_7[7:0], e}), .in2({e, data0_7[7:0], e, e}),
    .in3({data0_7[7:0], e, e, e}), .out(storebyte), .sel(MemAddress[1:0]));
  Multiplexer #(.select(2), .width(32)) multiplexer_2 (
    .in0({sixteen, data15_0[15:0]}), .in2({data15_0[15:0], sixteen}), .out(store_half), .sel(MemAddress[1:0]));  // open: in1, in3
  assign sixteen = {{15{1'b0}}, 1'b0};  // Bit_Extender bit_extender_3
  assign data15_0 = {{16{1'b0}}, DataFromReg[15:0]};  // Bit_Extender bit_extender_4
  assign e = {{7{1'b0}}, 1'b0};  // Bit_Extender bit_extender_5
  Comparator #(.width(3)) comparator_1 (.a(Instruction[14:12]), .b(3'b010), .eq(funct3_is_2));  // open: gt, lt
  Comparator #(.width(3)) comparator_2 (.a(Instruction[14:12]), .b(3'b000), .eq(funct3_is_0));  // open: gt, lt
  Comparator #(.width(3)) comparator_3 (.a(Instruction[14:12]), .b(3'b001), .eq(funct3_is_1));  // open: gt, lt
  Comparator #(.width(2)) comparator_4 (.a(MemAddress[1:0]), .b(2'b00), .eq(bot_0));  // open: gt, lt
  Comparator #(.width(2)) comparator_5 (.a(MemAddress[1:0]), .b(2'b01), .eq(bot_1));  // open: gt, lt
  Comparator #(.width(2)) comparator_6 (.a(MemAddress[1:0]), .b(2'b10), .eq(bot_2));  // open: gt, lt
  Comparator #(.width(2)) comparator_7 (.a(MemAddress[1:0]), .b(2'b11), .eq(bot_3));  // open: gt, lt
  Multiplexer #(.select(3), .width(32)) multiplexer_3 (
    .in0(storebyte), .in1(store_half), .in2(DataFromReg), .out(DataToMem), .sel(Instruction[14:12]));  // open: in3, in4, in5, in6, in7
  and and_1 (and_1_out, funct3_is_0, bot_2);
  and and_2 (and_2_out, funct3_is_1, bot_2);
  and and_3 (and_3_out, funct3_is_2, bot_0);
  and and_4 (and_4_out, funct3_is_0, bot_1);
  and and_5 (and_5_out, funct3_is_0, bot_0);
  and and_6 (and_6_out, funct3_is_0, bot_3);
  and and_7 (and_7_out, funct3_is_1, bot_0);
  Priority_Encoder #(.select_enc(4)) priority_encoder_1 (
    .in1(and_5_out), .in2(and_4_out), .in3(and_7_out), .in4(and_1_out), .in8(and_6_out), .in12(and_2_out),
    .in15(and_3_out), .out(priority_encoder_1_out));  // open: in0, in5, in6, in7, in9, in10, in11, in13, in14, gs, en_out, en_in
  Multiplexer #(.width(4)) multiplexer_4 (
    .in0(4'b0000), .in1(priority_encoder_1_out), .out(MemWriteMask), .sel(MemWEn));

  // Other names for the same wires on the sheet: funct3[2:0] = Instruction[14:12]; bot_two[1:0] = MemAddress[1:0]

  // Notes on the sheet:
  //   INPUTS to your circuit
  //   DON'T CHANGE THE LOCATIONS OF THE INPUTS AND OUTPUTS!
  //   OUTPUT from your circuit
endmodule
